// Digital circuit VecAddSub.dig as structural Verilog
module VecAddSub (
  input  [3:0] in_3,
  input  [3:0] in_4,
  input  in_5,
  input  [3:0] in_8,
  input  [3:0] in_9,
  input  in_10,
  input  [3:0] in_13,
  input  [3:0] in_14,
  input  in_15,
  input  [3:0] in_18,
  input  [3:0] in_19,
  input  in_20,
  input  [3:0] in_23,
  input  [3:0] in_24,
  input  in_25,
  input  [3:0] in_28,
  input  [3:0] in_29,
  input  in_30,
  input  [3:0] in_33,
  input  [3:0] in_34,
  input  in_35,
  input  [3:0] in_38,
  input  [3:0] in_39,
  input  in_40,
  input  [31:0] A_i,
  input  [31:0] B_i,
  input  mode,
  input  [1:0] vecSize_i,
  output [3:0] out_1,
  output out_2,
  output [3:0] out_6,
  output out_7,
  output [3:0] out_11,
  output out_12,
  output [3:0] out_16,
  output out_17,
  output [3:0] out_21,
  output out_22,
  output [3:0] out_26,
  output out_27,
  output [3:0] out_31,
  output out_32,
  output [3:0] out_36,
  output out_37,
  output [31:0] S_o
);

  VecAddSub #(.applicationType("IVERILOG")) u_VecAddSub (
    .A_i(A_i), .B_i(B_i), .mode_i(mode), .vecSize_i(vecSize_i), .S_o(S_o));
  Add #(.Bits(4)) add_1 (.a(in_13), .b(in_14), .c_i(in_15), .s(out_11), .c_o(out_12));
  Add #(.Bits(4)) add_2 (.a(in_18), .b(in_19), .c_i(in_20), .s(out_16), .c_o(out_17));
  Add #(.Bits(4)) add_3 (.a(in_33), .b(in_34), .c_i(in_35), .s(out_31), .c_o(out_32));
  Add #(.Bits(4)) add_4 (.a(in_38), .b(in_39), .c_i(in_40), .s(out_36), .c_o(out_37));
  Add #(.Bits(4)) add_5 (.a(in_3), .b(in_4), .c_i(in_5), .s(out_1), .c_o(out_2));
  Add #(.Bits(4)) add_6 (.a(in_8), .b(in_9), .c_i(in_10), .s(out_6), .c_o(out_7));
  Add #(.Bits(4)) add_7 (.a(in_23), .b(in_24), .c_i(in_25), .s(out_21), .c_o(out_22));
  Add #(.Bits(4)) add_8 (.a(in_28), .b(in_29), .c_i(in_30), .s(out_26), .c_o(out_27));
endmodule

/* Code of VecAddSub:
module AddSub4 (
    input  [3:0] A,
    input  [3:0] B,
    input        mode,     // 0: soma, 1: subtração
    input        cin,
    output [3:0] S,
    output       cout
);
    wire [3:0] B_xor = B ^ {4{mode}}; // Inverte B se for subtração
    assign {cout, S} = A + B_xor + cin;
endmodule

module VecAddSub (
    input  [31:0] A_i,
    input  [31:0] B_i,
    input         mode_i,
    input  [1:0]  vecSize_i,
    output [31:0] S_o
);
    wire [7:0][3:0] A_blocks, B_blocks, S_blocks;
    wire [7:0] cins, couts;
    genvar i;

    assign cins[0] = mode_i; // Cin = 1 for sub, 0 for add

    // Divide A and B into 8 blocks of 4 bits
    generate
        for (i = 0; i < 8; i = i + 1) begin
            assign A_blocks[i] = A_i[i*4 +: 4];
            assign B_blocks[i] = B_i[i*4 +: 4];

            AddSub4 addsub (
                .A   (A_blocks[i]),
                .B   (B_blocks[i]),
                .mode(mode_i),
                .cin (cins[i]),
                .S   (S_blocks[i]),
                .cout(couts[i])
            );

            // Define cins[i+1] with respect to vecSize_i
            if (i < 7) begin
                wire segment_boundary;
                assign segment_boundary = (vecSize_i == 2'b00 && (i % 1 == 0)) ||
                                          (vecSize_i == 2'b01 && (i % 2 == 1)) ||
                                          (vecSize_i == 2'b10 && (i % 4 == 3)) ||
                                          (vecSize_i == 2'b11);
                assign cins[i+1] = segment_boundary ? couts[i] : mode_i;
            end
        end
    endgenerate

    // Flatten output
    assign S_o = {S_blocks[7], S_blocks[6], S_blocks[5], S_blocks[4],
                  S_blocks[3], S_blocks[2], S_blocks[1], S_blocks[0]};
endmodule
*/
