// Digital circuit EEL580-CPU.dig as structural Verilog
module EEL580_CPU (
  input  CLK,
  input  in_2,
  input  [4:0] in_3
);

  wire FFD_nq, multiplexer_10_out, not_1_out, or_1_out, u_EXMEM_zeroout, u_Hazard_stall;
  wire [1:0] or_2_out, u_Control_Unit_aluop, u_Control_Unit_alusrc, u_Control_Unit_regsrc,
       u_Forward_forwarda, u_Forward_forwardb;
  wire [2:0] multiplexer_5_out, u_EXMEM_wbout, u_MEMWB_wbout;
  wire [2:2] u_Control_Unit_regwrite;
  wire [3:0] multiplexer_4_out, u_ALU_Control_control, u_IDEX_alucontrolout, u_IDEX_exout;
  wire [4:0] u_EXMEM_mout, u_EXMEM_wbadout, u_IDEX_rs1out, u_IDEX_rs2out, u_IDEX_wbadout, u_MEMWB_wbadout;
  wire [5:0] multiplexer_3_out, u_Control_Unit_memread, u_IDEX_mout;
  wire [7:0] Contador_out;
  wire [31:0] multiplexer_1_out, multiplexer_2_out, multiplexer_6_out, multiplexer_7_out, multiplexer_8_out,
       multiplexer_9_out, multiplexer_11_out, ramdualport_1_d, ROM_d, u_EXMEM_aluout, u_EXMEM_pcout,
       u_EXMEM_pcp4out, u_EXMEM_read2out, u_IDEX_immgenout, u_IDEX_pcout, u_IDEX_pcp4out, u_IDEX_read1out,
       u_IDEX_read2out, u_IDEX_wbout, u_IFID_instout, u_IFID_pcout, u_IFID_pcp4out, u_ImmGen_imm,
       u_MEMWB_aluout, u_MEMWB_pcp1out, u_MEMWB_pcp4out, u_MEMWB_readout, u_PC_pc_out, u_register_file_outa,
       u_register_file_outb, u_register_file_outregmanual, u_Somador_2_z, u_Somador_z;

  Multiplexer #(.Bits(32)) multiplexer_1 (
    .sel(FFD_nq), .in_0(multiplexer_2_out), .in_1(u_Somador_z), .out(multiplexer_1_out));
  D_FF FFD (.D(1'b0), .C(CLK), .nQ(FFD_nq));  // open: Q
  Counter #(.Bits(8)) Contador (.en(1'b1), .C(CLK), .clr(in_2), .out(Contador_out));  // open: ovf
  PC #(.applicationType("GHDL")) u_PC (
    .clk(Contador_out[0]), .rst(in_2), .writeEn(u_Hazard_stall), .PC_in(multiplexer_1_out),
    .PC_out(u_PC_pc_out));
  Somador #(.applicationType("GHDL")) u_Somador (.A(u_PC_pc_out), .B(32'h1), .Z(u_Somador_z));
  ROM #(.AddrBits(24), .Bits(32)) ROM (.A(u_PC_pc_out[23:0]), .sel(1'b1), .D(ROM_d));
  IFID #(.applicationType("GHDL")) u_IFID (
    .clk(Contador_out[0]), .writeEnable(u_Hazard_stall), .pcIn(u_PC_pc_out), .pcP4In(u_Somador_z),
    .instIn(ROM_d), .pcout(u_IFID_pcout), .pcP4out(u_IFID_pcp4out), .instOut(u_IFID_instout));
  // Probe Ponta de Prova on u_IFID_instout
  Hazard #(.applicationType("GHDL")) u_Hazard (
    .clk(CLK), .MemReadEX(u_IDEX_mout[0]), .RDEX(u_IDEX_wbadout), .RSrc1(u_IFID_instout[19:15]),
    .RSrc2(u_IFID_instout[24:20]), .stall(u_Hazard_stall));
  register_file #(.applicationType("GHDL")) u_register_file (
    .clk(CLK), .\input (multiplexer_11_out), .regSelA(u_IFID_instout[19:15]),
    .regSelB(u_IFID_instout[24:20]), .writeRegSel(u_MEMWB_wbadout), .regSelManual(in_3),
    .writeEnable(u_MEMWB_wbout[2]), .outA(u_register_file_outa), .outB(u_register_file_outb),
    .outRegManual(u_register_file_outregmanual));
  ImmGen #(.applicationType("GHDL")) u_ImmGen (.inst(u_IFID_instout), .imm(u_ImmGen_imm));
  Control_Unit #(.applicationType("GHDL")) u_Control_Unit (
    .opcode(u_IFID_instout[6:0]), .AluSrc(u_Control_Unit_alusrc[0]), .blockA(u_Control_Unit_alusrc[1]),
    .RegWrite(u_Control_Unit_regwrite[2]), .MemRead(u_Control_Unit_memread[0]),
    .MemWrite(u_Control_Unit_memread[1]), .Branch(u_Control_Unit_memread[2]),
    .BranchNotEq(u_Control_Unit_memread[3]), .BrIncond(u_Control_Unit_memread[4]),
    .regToPC(u_Control_Unit_memread[5]), .AluOp(u_Control_Unit_aluop), .regSrc(u_Control_Unit_regsrc));
  // Probe Ponta de Prova on u_register_file_outregmanual
  Multiplexer #(.Selector_Bits(2), .Bits(32)) multiplexer_2 (
    .sel(or_2_out), .in_0(u_Somador_z), .in_1(u_EXMEM_pcout), .in_2(u_EXMEM_aluout), .in_3(u_EXMEM_aluout),
    .out(multiplexer_2_out));
  IDEX #(.applicationType("GHDL")) u_IDEX (
    .clk(Contador_out[0]), .pcIn(u_IFID_pcout), .read1In(u_register_file_outa),
    .read2In(u_register_file_outb), .immGenIn(u_ImmGen_imm),
    .aluControlIn({u_IFID_instout[30], u_IFID_instout[14:12]}), .wbadIn(u_IFID_instout[11:7]),
    .WBIn(multiplexer_5_out), .MIn(multiplexer_3_out), .EXin(multiplexer_4_out), .pcP4In(u_IFID_pcp4out),
    .rs1In(u_IFID_instout[19:15]), .rs2In(u_IFID_instout[24:20]), .pcOut(u_IDEX_pcout),
    .read1Out(u_IDEX_read1out), .read2Out(u_IDEX_read2out), .immGenOut(u_IDEX_immgenout),
    .aluControlOut(u_IDEX_alucontrolout), .wbadOut(u_IDEX_wbadout), .WBOut(u_IDEX_wbout[2:0]),
    .MOut(u_IDEX_mout), .EXOut(u_IDEX_exout), .pcP4Out(u_IDEX_pcp4out), .rs1Out(u_IDEX_rs1out),
    .rs2Out(u_IDEX_rs2out));
  Multiplexer #(.Bits(6)) multiplexer_3 (
    .sel(u_Hazard_stall), .in_0(u_Control_Unit_memread), .in_1({6{1'b0}}), .out(multiplexer_3_out));
  Multiplexer #(.Bits(4)) multiplexer_4 (
    .sel(u_Hazard_stall), .in_0({u_Control_Unit_aluop, u_Control_Unit_alusrc}), .in_1(4'b0000),
    .out(multiplexer_4_out));
  Multiplexer #(.Bits(3)) multiplexer_5 (
    .sel(u_Hazard_stall), .in_0({u_Control_Unit_regwrite[2], u_Control_Unit_regsrc}), .in_1(3'b000),
    .out(multiplexer_5_out));
  Multiplexer #(.Bits(32)) multiplexer_6 (
    .sel(u_IDEX_exout[1]), .in_0(u_IDEX_read1out), .in_1({32{1'b0}}), .out(multiplexer_6_out));
  Multiplexer #(.Bits(32)) multiplexer_7 (
    .sel(u_IDEX_exout[0]), .in_0(u_IDEX_read2out), .in_1(u_IDEX_immgenout), .out(multiplexer_7_out));
  Multiplexer #(.Selector_Bits(2), .Bits(32)) multiplexer_8 (
    .sel(u_Forward_forwarda), .in_0(multiplexer_6_out), .in_1(multiplexer_11_out), .in_2(u_EXMEM_aluout),
    .in_3({32{1'b0}}), .out(multiplexer_8_out));
  Multiplexer #(.Selector_Bits(2), .Bits(32)) multiplexer_9 (
    .sel(u_Forward_forwardb), .in_0(multiplexer_7_out), .in_1(multiplexer_11_out), .in_2(u_EXMEM_aluout),
    .in_3({32{1'b0}}), .out(multiplexer_9_out));
  Somador #(.applicationType("GHDL")) u_Somador_2 (.A(u_IDEX_pcout), .B(u_IDEX_immgenout), .Z(u_Somador_2_z));
  ALU #(.applicationType("GHDL")) u_ALU (
    .A(multiplexer_8_out), .B(multiplexer_9_out), .control(u_ALU_Control_control), .zero(u_IDEX_wbout[0]));  // open: result
  ALU_Control #(.applicationType("GHDL")) u_ALU_Control (.Control(u_ALU_Control_control));  // open: Functs, AluOp
  EXMEM #(.applicationType("GHDL")) u_EXMEM (
    .clk(Contador_out[0]), .sumIn(u_Somador_2_z), .zeroIn(u_IDEX_wbout[0]), .aluIn(u_IDEX_wbout),
    .read2In(u_IDEX_read2out), .wbadIn(u_IDEX_wbadout), .WBIn(u_IDEX_wbout[2:0]), .MIn(u_IDEX_mout),
    .pcP4In(u_IDEX_pcp4out), .pcOut(u_EXMEM_pcout), .pcP4Out(u_EXMEM_pcp4out), .zeroOut(u_EXMEM_zeroout),
    .aluOut(u_EXMEM_aluout), .read2Out(u_EXMEM_read2out), .wbadOut(u_EXMEM_wbadout), .WBOut(u_EXMEM_wbout),
    .MOut({or_2_out[1], u_EXMEM_mout}));
  Forward #(.applicationType("GHDL")) u_Forward (
    .clk(CLK), .regWriteMEM(u_EXMEM_wbout[0]), .regWriteWB(u_MEMWB_wbout[0]), .RSrc1(u_IDEX_rs1out),
    .RSrc2(u_IDEX_rs2out), .RDMEM(u_EXMEM_wbadout), .RDWB(u_MEMWB_wbadout), .forwardA(u_Forward_forwarda),
    .forwardB(u_Forward_forwardb));
  or or_1 (or_1_out, u_EXMEM_mout[2], u_EXMEM_mout[3]);
  or or_2 (or_2_out[0], u_EXMEM_mout[4], u_EXMEM_pcout[0]);
  and and_1 (u_EXMEM_pcout[0], or_1_out, multiplexer_10_out);
  Multiplexer multiplexer_10 (
    .sel(u_EXMEM_mout[3]), .in_0(u_EXMEM_zeroout), .in_1(not_1_out), .out(multiplexer_10_out));
  not not_1 (not_1_out, u_EXMEM_zeroout);
  RAMDualPort #(.AddrBits(24), .Bits(32)) ramdualport_1 (
    .A(u_EXMEM_aluout[23:0]), .Din(u_EXMEM_read2out), .str(u_EXMEM_mout[1]), .C(CLK), .ld(u_EXMEM_mout[0]),
    .D(ramdualport_1_d));
  MEMWB #(.applicationType("GHDL")) u_MEMWB (
    .clk(Contador_out[0]), .readIn(ramdualport_1_d), .aluIn(u_EXMEM_aluout), .wbadIn(u_EXMEM_wbadout),
    .WBIn(u_EXMEM_wbout), .pcP4In(u_EXMEM_pcp4out), .pcP1In(u_EXMEM_pcout), .readOut(u_MEMWB_readout),
    .aluOut(u_MEMWB_aluout), .wbadOut(u_MEMWB_wbadout), .WBOut(u_MEMWB_wbout), .pcP4Out(u_MEMWB_pcp4out),
    .pcP1Out(u_MEMWB_pcp1out));
  Multiplexer #(.Selector_Bits(2), .Bits(32)) multiplexer_11 (
    .sel(u_MEMWB_wbout[1:0]), .in_0(u_MEMWB_aluout), .in_1(u_MEMWB_readout), .in_2(u_MEMWB_pcp4out),
    .in_3(u_MEMWB_pcp1out), .out(multiplexer_11_out));
  // Pins of 1 and 32 bits meet at u_EXMEM_pcout
  // Pins of 1 and 3 and 32 bits meet at u_IDEX_wbout
endmodule

/* Code of PC:
library IEEE;
use IEEE.STD_LOGIC_1164.ALL;
use IEEE.NUMERIC_STD.ALL;

entity PC is
    Port (
        clk     : in  STD_LOGIC;                     -- Clock
        rst     : in  STD_LOGIC;                     -- Reset síncrono
        writeEn : in  STD_LOGIC;                     -- Habilitação de escrita
        PC_in   : in  STD_LOGIC_VECTOR(31 downto 0); -- Próximo valor do PC
        PC_out  : out STD_LOGIC_VECTOR(31 downto 0)  -- Valor atual do PC
    );
end PC;

architecture Behavioral of PC is
    signal PC_reg : STD_LOGIC_VECTOR(31 downto 0);
begin

    process(clk)
    begin
        if rising_edge(clk) then
            if rst = '1' then -- zera o PC caso reset for ativado
                PC_reg <= (others => '0');
            elsif writeEn = '1' then -- atualiza o PC writeEn estiver habilitado
                PC_reg <= PC_in;
            end if;
        end if;
    end process;

    PC_out <= PC_reg;

end Behavioral;
*/

/* Code of Somador:
library IEEE;
use IEEE.STD_LOGIC_1164.ALL;
use IEEE.NUMERIC_STD.ALL;

entity Somador is
    Port (
        A : in  STD_LOGIC_VECTOR(31 downto 0);  -- Entrada A
        B : in  STD_LOGIC_VECTOR(31 downto 0);  -- Entrada B
        Z : out STD_LOGIC_VECTOR(31 downto 0)   -- Saída Z (A + B)
    );
end Somador;

architecture Behavioral of Somador is
begin
    -- Atribuição direta: Z é a soma de A e B
    Z <= std_logic_vector(unsigned(A) + unsigned(B));
end Behavioral;
*/

/* Code of IFID:
library IEEE;
use IEEE.STD_LOGIC_1164.ALL;
use IEEE.NUMERIC_STD.ALL;

entity IFID is
    Port (
        clk          : in  STD_LOGIC;
        writeEnable  : in  STD_LOGIC;
        pcIn         : in  STD_LOGIC_VECTOR(31 downto 0);
        pcP4In       : in  STD_LOGIC_VECTOR(31 downto 0);
        instIn       : in  STD_LOGIC_VECTOR(31 downto 0);
        pcout        : out STD_LOGIC_VECTOR(31 downto 0);
        pcP4out      : out STD_LOGIC_VECTOR(31 downto 0);
        instOut      : out STD_LOGIC_VECTOR(31 downto 0)
    );
end IFID;

architecture Behavioral of IFID is
    signal IDIF : STD_LOGIC_VECTOR(95 downto 0); -- registrador do pipeline
begin

    process(clk)
    begin
        -- Borda de subida: armazena dados no pipeline
        if rising_edge(clk) then
            if writeEnable = '0' then
                -- Guardar a instrução
                IDIF(31 downto 0)   <= instIn;

                -- Guardar PC atual
                IDIF(63 downto 32)  <= pcIn;

                -- Guardar PC + 4
                IDIF(95 downto 64)  <= pcP4In;
            end if;
        end if;

        -- Borda de descida: envia dados armazenados para os estágios seguintes
        if falling_edge(clk) then
            -- Saída do PC atual
            pcout     <= IDIF(63 downto 32);

            -- Saída da instrução
            instOut   <= IDIF(31 downto 0);

            -- Saída do PC + 4
            pcP4out   <= IDIF(95 downto 64);
        end if;
    end process;

end Behavioral;
*/

/* Code of Hazard:
library IEEE;
use IEEE.std_logic_1164.all;

entity Hazard is
    port (
        clk       : in  std_logic;
        MemReadEX : in  std_logic;
        RDEX      : in  std_logic_vector(4 downto 0);
        RSrc1     : in  std_logic_vector(4 downto 0);
        RSrc2     : in  std_logic_vector(4 downto 0);
        stall     : out std_logic
    );
end entity Hazard;

architecture Behavioral of Hazard is
    signal stall_interno : std_logic := '0';
begin
    process(clk)
    begin
        if rising_edge(clk) then
            if (MemReadEX = '1') and ((RDEX = RSrc1) or (RDEX = RSrc2)) then
                stall_interno <= '1';  -- Aplica stall se houver dependência
            else
                stall_interno <= '0';  -- Caso contrário, continua normal
            end if;
        end if;
    end process;

    stall <= stall_interno;
end architecture Behavioral;
*/

/* Code of register_file:
library IEEE;
use IEEE.STD_LOGIC_1164.ALL;
use IEEE.NUMERIC_STD.ALL;

entity register_file is
    Port (
        clk           : in  STD_LOGIC;
        input         : in  STD_LOGIC_VECTOR(31 downto 0);
        regSelA       : in  STD_LOGIC_VECTOR(4 downto 0);
        regSelB       : in  STD_LOGIC_VECTOR(4 downto 0);
        writeRegSel   : in  STD_LOGIC_VECTOR(4 downto 0);
        regSelManual  : in  STD_LOGIC_VECTOR(4 downto 0);
        writeEnable   : in  STD_LOGIC;
        outA          : out STD_LOGIC_VECTOR(31 downto 0);
        outB          : out STD_LOGIC_VECTOR(31 downto 0);
        outRegManual  : out STD_LOGIC_VECTOR(31 downto 0)
    );
end register_file;

architecture Behavioral of register_file is
    type reg_array is array (0 to 31) of STD_LOGIC_VECTOR(31 downto 0);
    signal registers : reg_array := (others => (others => '0'));
begin

    process(clk)
    begin
        if rising_edge(clk) then
            -- Leitura de A
            if registers(to_integer(unsigned(regSelA))) = "UUUUUUUUUUUUUUUUUUUUUUUUUUUUUUUU" then
                outA <= (others => '0');  -- Caso 'U', retorna zero
            else
                outA <= registers(to_integer(unsigned(regSelA)));
            end if;

            -- Leitura de B
            if registers(to_integer(unsigned(regSelB))) = "UUUUUUUUUUUUUUUUUUUUUUUUUUUUUUUU" then
                outB <= (others => '0');
            else
                outB <= registers(to_integer(unsigned(regSelB)));
            end if;
        end if;
    end process;

    -- Escrita na borda de descida + bypass
    process(clk)
    begin
        if falling_edge(clk) then
            if writeEnable = '1' then
                registers(to_integer(unsigned(writeRegSel))) <= input;

                -- Bypass para leitura A
                if regSelA = writeRegSel then
                    outA <= input;
                end if;

                -- Bypass para leitura B
                if regSelB = writeRegSel then
                    outB <= input;
                end if;
            end if;
        end if;
    end process;

    -- Leitura manual de um registrador
    outRegManual <= registers(to_integer(unsigned(regSelManual)));

end Behavioral;
*/

/* Code of ImmGen:
library IEEE;
use IEEE.STD_LOGIC_1164.ALL;
use IEEE.NUMERIC_STD.ALL;

entity ImmGen is
    Port (
        inst : in  STD_LOGIC_VECTOR(31 downto 0);  -- Instrução completa (32 bits)
        imm  : out STD_LOGIC_VECTOR(31 downto 0)   -- Imediato estendido
    );
end ImmGen;

architecture Behavioral of ImmGen is
    signal opcode : STD_LOGIC_VECTOR(6 downto 0);
begin
    opcode <= inst(6 downto 0);

    process(inst, opcode)
        variable imm_temp : signed(31 downto 0);
    begin
        case opcode is

            -- Tipo I (ex: addi, lw)
            when "0010011" | "0000011" | "1100111" =>
                imm_temp := resize(signed(inst(31 downto 20)), 32);

            -- Tipo S (ex: sw)
            when "0100011" =>
                imm_temp := resize(signed(inst(31 downto 25) & inst(11 downto 7)), 32);

            -- Tipo B (ex: beq, bne)
            when "1100011" =>
                imm_temp := resize(signed(
                    inst(31) &          -- bit 12 (MSB)
                    inst(7) &           -- bit 11
                    inst(30 downto 25) &-- bits 10-5
                    inst(11 downto 8) & -- bits 4-1
                    '0'                 -- LSB sempre zero (byte-aligned)
                ), 32);

            -- Tipo U (ex: lui, auipc)
            when "0110111" | "0010111" =>
                imm_temp := signed(inst(31 downto 12) & x"000");

            -- Tipo J (ex: jal)
            when "1101111" =>
                imm_temp := resize(signed(
                    inst(31) &                  -- bit 20
                    inst(19 downto 12) &        -- bits 19-12
                    inst(20) &                  -- bit 11
                    inst(30 downto 21) &        -- bits 10-1
                    '0'                         -- LSB
                ), 32);

            -- Default: zero
            when others =>
                imm_temp := (others => '0');

        end case;

        imm <= std_logic_vector(imm_temp);
    end process;

end Behavioral;
*/

/* Code of Control_Unit:
library IEEE;
use IEEE.STD_LOGIC_1164.ALL;

entity Control_Unit is
    port(
        opcode                     : in  std_logic_vector(6 downto 0);
        AluSrc, blockA, RegWrite   : out std_logic;
        MemRead, MemWrite, Branch  : out std_logic;
        BranchNotEq, BrIncond      : out std_logic;
        regToPC                    : out std_logic;
        AluOp, regSrc              : out std_logic_vector(1 downto 0)
    );
end Control_Unit;

architecture Behavioral of Control_Unit is
begin
    process(opcode)
    begin
        -- Valores padrão (para segurança)
        AluSrc      <= '0';
        blockA      <= '0';
        RegWrite    <= '0';
        MemRead     <= '0';
        MemWrite    <= '0';
        Branch      <= '0';
        BranchNotEq <= '0';
        BrIncond    <= '0';
        regToPC     <= '0';
        AluOp       <= "00";
        regSrc      <= "00";

        case opcode is
            -- Tipo R (add, sub, etc.)
            when "0110011" =>
                AluSrc   <= '0';
                blockA   <= '0';
                RegWrite <= '1';
                AluOp    <= "10";
                regSrc   <= "00";

            -- Tipo I (addi, andi, etc.)
            when "0010011" =>
                AluSrc   <= '1';
                blockA   <= '0';
                RegWrite <= '1';
                AluOp    <= "11";
                regSrc   <= "00";

            -- Tipo S (sw)
            when "0100011" =>
                AluSrc    <= '1';
                blockA    <= '0';
                RegWrite  <= '0';
                MemWrite  <= '1';
                AluOp     <= "00";
                regSrc    <= "00";

            -- Tipo I (lw)
            when "0000011" =>
                AluSrc    <= '1';
                blockA    <= '0';
                RegWrite  <= '1';
                MemRead   <= '1';
                AluOp     <= "00";
                regSrc    <= "00";

            -- beq
            when "1100111" =>
                AluSrc    <= '0';
                blockA    <= '0';
                Branch    <= '1';
                AluOp     <= "01";
                regSrc    <= "00";

            -- bne
            when "1100011" =>
                AluSrc       <= '0';
                blockA       <= '0';
                Branch       <= '1';
                BranchNotEq  <= '1';
                AluOp        <= "01";
                regSrc       <= "00";

            -- jal
            when "1101111" =>
                AluSrc    <= '1';
                blockA    <= '1';
                RegWrite  <= '1';
                BrIncond  <= '1';
                regToPC   <= '1';
                AluOp     <= "00";
                regSrc    <= "10";

            when others =>
                -- Mantém valores padrão (instrução inválida ou não implementada)
                null;
        end case;
    end process;
end Behavioral;
*/

/* Code of IDEX:
library IEEE;
use IEEE.std_logic_1164.all;
use IEEE.numeric_std.all;

entity IDEX is
    port (
        clk          : in  std_logic;
        pcIn         : in  std_logic_vector(31 downto 0);
        read1In      : in  std_logic_vector(31 downto 0);
        read2In      : in  std_logic_vector(31 downto 0);
        immGenIn     : in  std_logic_vector(31 downto 0);
        aluControlIn : in  std_logic_vector(3 downto 0);
        wbadIn       : in  std_logic_vector(4 downto 0);
        WBIn         : in  std_logic_vector(2 downto 0);
        MIn          : in  std_logic_vector(5 downto 0);
        EXin         : in  std_logic_vector(3 downto 0);
        pcP4In       : in  std_logic_vector(31 downto 0);
        rs1In        : in  std_logic_vector(4 downto 0);
        rs2In        : in  std_logic_vector(4 downto 0);
        
        pcOut        : out std_logic_vector(31 downto 0);
        read1Out     : out std_logic_vector(31 downto 0);
        read2Out     : out std_logic_vector(31 downto 0);
        immGenOut    : out std_logic_vector(31 downto 0);
        aluControlOut: out std_logic_vector(3 downto 0);
        wbadOut      : out std_logic_vector(4 downto 0);
        WBOut        : out std_logic_vector(2 downto 0);
        MOut         : out std_logic_vector(5 downto 0);
        EXOut        : out std_logic_vector(3 downto 0);
        pcP4Out      : out std_logic_vector(31 downto 0);
        rs1Out       : out std_logic_vector(4 downto 0);
        rs2Out       : out std_logic_vector(4 downto 0)
    );
end entity IDEX;

architecture Behavioral of IDEX is
    signal idex_s : std_logic_vector(191 downto 0);
begin
    process(clk)
    begin
        if rising_edge(clk) then
            idex_s(31 downto 0)    <= pcIn;
            idex_s(63 downto 32)   <= read1In;
            idex_s(95 downto 64)   <= read2In;
            idex_s(127 downto 96)  <= immGenIn;
            idex_s(131 downto 128) <= aluControlIn;
            idex_s(136 downto 132) <= wbadIn;
            idex_s(139 downto 137) <= WBIn;
            idex_s(145 downto 140) <= MIn;
            idex_s(149 downto 146) <= EXin;
            idex_s(181 downto 150) <= pcP4In;
            idex_s(186 downto 182) <= rs1In;
            idex_s(191 downto 187) <= rs2In;
        elsif falling_edge(clk) then
            pcOut         <= idex_s(31 downto 0);
            read1Out      <= idex_s(63 downto 32);
            read2Out      <= idex_s(95 downto 64);
            immGenOut     <= idex_s(127 downto 96);
            aluControlOut <= idex_s(131 downto 128);
            wbadOut       <= idex_s(136 downto 132);
            WBOut         <= idex_s(139 downto 137);
            MOut          <= idex_s(145 downto 140);
            EXOut         <= idex_s(149 downto 146);
            pcP4Out       <= idex_s(181 downto 150);
            rs1Out        <= idex_s(186 downto 182);
            rs2Out        <= idex_s(191 downto 187);
        end if;
    end process;
end architecture Behavioral;
*/

/* Code of ALU:
library IEEE;
use IEEE.STD_LOGIC_1164.ALL;
use ieee.numeric_std.ALL;
USE IEEE.std_logic_unsigned.ALL;

-- A ALU FAZ A OPERAÇÃO INDICADA NO SINAL DE CONTROLE. ELA FAZ A + B, A - B, A OR B, A AND B, SHIFT LEFT E SHIFT RIGHT. A OPERAÇÃO DE SHIFT É MULTIPLICAR POR 2 (QND SHIFT RIGHT) E DIVIDIR POR 2 QUANDO É SHIFT LEFT.ESCIFICAR OS CÓDIGOS DA OPERAÇÃO.

entity ALU is
    port(
    A, B       : in std_logic_vector(31 downto 0);  -- Entradas A e B de 32 bits
    control   : in std_logic_vector(3 downto 0);   -- Entrada de controle de 4 bits que seleciona a operação
    result    : out std_logic_vector(31 downto 0); -- Saída de resultado de 32 bits
    zero      : out std_logic);                    -- Saída para sinalizar se o resultado é zero
end ALU;

architecture TypeArchitecture of ALU is

signal zero_out   : std_logic_vector(32 downto 0); -- Vetor para verificação de resultado zero
signal result_out : std_logic_vector(31 downto 0); -- Vetor para armazenar o resultado da operação

begin
	
    result_out <= (A + B) when control = "0010" else                  -- Soma
    			   (A - B) when control = "0110" else                  -- Subtração
    			   (A XOR B) when control = "0101" else                -- XOR (ou exclusivo)
    			   (A OR B) when control = "0001" else                 -- OR (ou)
    			   (A AND B) when control = "0000" else                -- AND (e)
    			   (std_logic_vector(shift_left(unsigned(A), to_integer(unsigned(B))))) when control = "0011" else   -- Shift Left (deslocamento à esquerda)
    			   (std_logic_vector(shift_right(unsigned(A), to_integer(unsigned(B))))) when control = "0111";    -- Shift Right (deslocamento à direita)
        			
    result <= result_out;                          -- Atribui o valor do resultado à saída result
    zero_out(0) <= '0';                            -- Inicializa o primeiro bit de zero_out como '0'
    G2: for I in 1 to 32 generate
            zero_out(I) <= zero_out(I - 1) or result_out(I - 1);  -- Verificação de resultado zero bit a bit
    end generate;
    zero <= not zero_out(32);                      -- Sinaliza se o resultado é zero (se zero_out(32) for '0', zero é '1', caso contrário, zero é '0')
end TypeArchitecture;
*/

/* Code of ALU_Control:
library IEEE;
use IEEE.STD_LOGIC_1164.ALL;

entity ALU_Control is
    port(
        Functs    : IN std_logic_vector(3 downto 0);    -- Entrada de códigos de função da ALU (4 bits)
        AluOp   : IN std_logic_vector(1 downto 0);      -- Entrada de códigos de operação da ALU (2 bits)
        Control : OUT std_logic_vector(3 downto 0)      -- Saída do controle da ALU (4 bits)
        );
end ALU_Control;

architecture TypeArchitecture of ALU_Control is
begin

	control <= "0010" when AluOp = "00" else -- Se AluOp for "00", Control recebe "0010" (Operação: Soma)
			 "0110" when AluOp = "01" else -- Se AluOp for "01", Control recebe "0110" (Operação: Branch)
			 "0010" when Functs = "0000" else -- Se Functs for "0000", Control recebe "0010" (Operação: Adição)
			 "0110" when Functs = "1000" else -- Se Functs for "1000", Control recebe "0110" (Operação: Subtração)
			 "0011" when Functs = "0001" else -- Se Functs for "0001", Control recebe "0011" (Operação: Shift Left)
			 "0101" when Functs = "0100" else -- Se Functs for "0100", Control recebe "0101" (Operação: XOR)
			 "0111" when Functs = "0101" else -- Se Functs for "0101", Control recebe "0111" (Operação: Shift Right)
			 "0001" when Functs = "0110" else -- Se Functs for "0110", Control recebe "0001" (Operação: OR)
			 "0000" when Functs = "0111"; -- Se Functs for "0111", Control recebe "0000" (Operação: AND)
	 
end TypeArchitecture;
*/

/* Code of EXMEM:
library IEEE;
use IEEE.std_logic_1164.all;
use IEEE.numeric_std.all;

entity EXMEM is
    port (
        clk        : in  std_logic;
        sumIn      : in  std_logic_vector(31 downto 0);
        zeroIn     : in  std_logic;
        aluIn      : in  std_logic_vector(31 downto 0);
        read2In    : in  std_logic_vector(31 downto 0);
        wbadIn     : in  std_logic_vector(4 downto 0);
        WBIn       : in  std_logic_vector(2 downto 0);
        MIn        : in  std_logic_vector(5 downto 0);
        pcP4In     : in  std_logic_vector(31 downto 0);

        pcOut      : out std_logic_vector(31 downto 0);
        pcP4Out    : out std_logic_vector(31 downto 0);
        zeroOut    : out std_logic;
        aluOut     : out std_logic_vector(31 downto 0);
        read2Out   : out std_logic_vector(31 downto 0);
        wbadOut    : out std_logic_vector(4 downto 0);
        WBOut      : out std_logic_vector(2 downto 0);
        MOut       : out std_logic_vector(5 downto 0)
    );
end entity EXMEM;

architecture Behavioral of EXMEM is
    signal exmem_s : std_logic_vector(142 downto 0);
begin
    process(clk)
    begin
        if rising_edge(clk) then
            exmem_s(31 downto 0)     <= sumIn;
            exmem_s(32)              <= zeroIn;
            exmem_s(64 downto 33)    <= aluIn;
            exmem_s(96 downto 65)    <= read2In;
            exmem_s(101 downto 97)   <= wbadIn;
            exmem_s(104 downto 102)  <= WBIn;
            exmem_s(110 downto 105)  <= MIn;
            exmem_s(142 downto 111)  <= pcP4In;
        end if;
    end process;

    -- Atribuições das saídas
    pcOut     <= exmem_s(31 downto 0);
    zeroOut   <= exmem_s(32);
    aluOut    <= exmem_s(64 downto 33);
    read2Out  <= exmem_s(96 downto 65);
    wbadOut   <= exmem_s(101 downto 97);
    WBOut     <= exmem_s(104 downto 102);
    MOut      <= exmem_s(110 downto 105);
    pcP4Out   <= exmem_s(142 downto 111);

end architecture Behavioral;
*/

/* Code of Forward:
library IEEE;
use IEEE.std_logic_1164.all;

entity Forward is
    port (
        clk         : in  std_logic;
        regWriteMEM : in  std_logic;
        regWriteWB  : in  std_logic;
        RSrc1       : in  std_logic_vector(4 downto 0);
        RSrc2       : in  std_logic_vector(4 downto 0);
        RDMEM       : in  std_logic_vector(4 downto 0);
        RDWB        : in  std_logic_vector(4 downto 0);
        forwardA    : out std_logic_vector(1 downto 0);
        forwardB    : out std_logic_vector(1 downto 0)
    );
end entity Forward;

architecture TypeArchitecture of Forward is
    signal forwardA_interno, forwardB_interno : std_logic_vector(1 downto 0) := "00";
begin
    process(clk)
    begin
        if rising_edge(clk) then
            -- Encaminhamento da fase MEM para a fonte A
            if (regWriteMEM = '1') and (RDMEM /= "00000") and (RDMEM = RSrc1) then
                forwardA_interno <= "10";
            end if;

            -- Encaminhamento da fase MEM para a fonte B
            if (regWriteMEM = '1') and (RDMEM /= "00000") and (RDMEM = RSrc2) then
                forwardB_interno <= "10";
            end if;

            -- Encaminhamento da fase WB para a fonte A
            if (regWriteWB = '1') and (RDWB /= "00000") and (RDWB = RSrc1) then
                forwardA_interno <= "01";
            end if;

            -- Encaminhamento da fase WB para a fonte B
            if (regWriteWB = '1') and (RDWB /= "00000") and (RDWB = RSrc2) then
                forwardB_interno <= "01";
            end if;
        end if;
    end process;

    -- Atribuições finais às saídas
    forwardA <= forwardA_interno;
    forwardB <= forwardB_interno;

end architecture TypeArchitecture;
*/

/* Code of MEMWB:
library IEEE;
use IEEE.std_logic_1164.all;
use IEEE.numeric_std.all;

entity MEMWB is
    port (
        clk       : in  std_logic;
        readIn    : in  std_logic_vector(31 downto 0);
        aluIn     : in  std_logic_vector(31 downto 0);
        wbadIn    : in  std_logic_vector(4 downto 0);
        WBIn      : in  std_logic_vector(2 downto 0);
        pcP4In    : in  std_logic_vector(31 downto 0);
        pcP1In    : in  std_logic_vector(31 downto 0);

        readOut   : out std_logic_vector(31 downto 0);
        aluOut    : out std_logic_vector(31 downto 0);
        wbadOut   : out std_logic_vector(4 downto 0);
        WBOut     : out std_logic_vector(2 downto 0);
        pcP4Out   : out std_logic_vector(31 downto 0);
        pcP1Out   : out std_logic_vector(31 downto 0)
    );
end entity MEMWB;

architecture Behavioral of MEMWB is
    signal memwb_s : std_logic_vector(135 downto 0);
begin
    process(clk)
    begin
        if rising_edge(clk) then
            memwb_s(31 downto 0)    <= readIn;
            memwb_s(63 downto 32)   <= aluIn;
            memwb_s(68 downto 64)   <= wbadIn;
            memwb_s(71 downto 69)   <= WBIn;
            memwb_s(103 downto 72)  <= pcP4In;
            memwb_s(135 downto 104) <= pcP1In;
        elsif falling_edge(clk) then
            readOut  <= memwb_s(31 downto 0);
            aluOut   <= memwb_s(63 downto 32);
            wbadOut  <= memwb_s(68 downto 64);
            WBOut    <= memwb_s(71 downto 69);
            pcP4Out  <= memwb_s(103 downto 72);
            pcP1Out  <= memwb_s(135 downto 104);
        end if;
    end process;
end architecture Behavioral;
*/
